# Fritzing sketch FOCUSarduino (saved by Fritzing 0.9.3b)
breadboards: 1

parts:
  元件1 = Arduino Uno (Rev3)
  hc-sr1 = hc-sr04

nets:
  N1: 元件1.D2, hc-sr1.Trig
  N2: 元件1.D3_PWM, hc-sr1.Echo
  5V: 元件1.5V, hc-sr1.VCC
  GND: 元件1.GND, hc-sr1.GND
